// Logisim project Lab06part2.circ as structural Verilog: 1 circuit, main circuit main
module main (
  input  Carry,
  input  [7:0] A,
  input  [7:0] B,
  input  Op,
  output [7:0] out_5,
  output [7:0] out_6,
  output [7:0] out_7
);

  Subtractor subtractor_1 (.a(A), .b(B), .out(out_6), .bin(Carry));  // open: bout
  Adder adder_1 (.a(A), .b(B), .out(out_5), .cin(Carry));  // open: cout
  Multiplexer #(.width(8)) multiplexer_1 (.in0(out_5), .in1(out_6), .out(out_7), .sel(Op));  // open: en
endmodule
