// Logisim project lab07part2.circ as structural Verilog: 2 circuits, main circuit main
module main (
  input  [7:0] in_1,
  output out_2
);

  wire bcddisplay_1_a, bcddisplay_1_b, bcddisplay_1_c, bcddisplay_1_d, bcddisplay_1_e, bcddisplay_1_f,
       bcddisplay_1_g, bcddisplay_1_h, bcddisplay_2_a, bcddisplay_2_b, bcddisplay_2_c, bcddisplay_2_d,
       bcddisplay_2_e, bcddisplay_2_f, bcddisplay_2_g, bcddisplay_2_h;

  BCDDisplay bcddisplay_1 (
    .in_1(in_1[7:4]), .A(bcddisplay_1_a), .B(bcddisplay_1_b), .C(bcddisplay_1_c), .D(bcddisplay_1_d),
    .E(bcddisplay_1_e), .F(bcddisplay_1_f), .G(bcddisplay_1_g), .H(bcddisplay_1_h));
  _7_Segment_Display u_7_segment_display_1 (
    .g(bcddisplay_1_a), .f(bcddisplay_1_b), .a(bcddisplay_1_c), .b(bcddisplay_1_d), .e(bcddisplay_1_e),
    .d(bcddisplay_1_f), .c(bcddisplay_1_g), .dp(bcddisplay_1_h));
  BCDDisplay bcddisplay_2 (
    .in_1(in_1[3:0]), .A(bcddisplay_2_a), .B(bcddisplay_2_b), .C(bcddisplay_2_c), .D(bcddisplay_2_d),
    .E(bcddisplay_2_e), .F(bcddisplay_2_f), .G(bcddisplay_2_g), .H(bcddisplay_2_h));
  _7_Segment_Display u_7_segment_display_2 (
    .g(bcddisplay_2_a), .f(bcddisplay_2_b), .a(bcddisplay_2_c), .b(bcddisplay_2_d), .e(bcddisplay_2_e),
    .d(bcddisplay_2_f), .c(bcddisplay_2_g), .dp(bcddisplay_2_h));
endmodule

module BCDDisplay (
  input  [3:0] in_1,
  output A,
  output B,
  output C,
  output D,
  output E,
  output F,
  output G,
  output H
);

  wire b1_nb0_out, b1b0_out, b2_nb1_2_out, b2_nb1_out, b2_nb1b0_out, b2b0_out, b2b1_nb0_out, b3b1_2_out,
       b3b1_out, b3b2_out, nb1_nb0_out, nb2_nb1_nb0_out, nb2_nb1_out, nb2b1_out, nb3_nb1_nb0_out,
       nb3_nb1_out, nb3_nb2_nb0_out, nb3_nb2_out, nb3_nb2b1_out, nb3b0_out, nb3b1b0_out, nb3b2_out,
       not_1_out, not_2_out, not_3_out, not_4_out;

  // AND_Gate and_1 is placed but not wired
  not not_1 (not_1_out, in_1[3]);
  not not_2 (not_2_out, in_1[1]);
  not not_3 (not_3_out, in_1[2]);
  not not_4 (not_4_out, in_1[0]);
  and nb2b1 (nb2b1_out, in_1[1], not_3_out);
  and b1_nb0 (b1_nb0_out, in_1[1], not_4_out);
  and b2_nb1 (b2_nb1_out, in_1[2], not_2_out);
  and nb1_nb0 (nb1_nb0_out, not_2_out, not_4_out);
  and b2_nb1_2 (b2_nb1_2_out, not_2_out, in_1[2]);
  and b2b1_nb0 (b2b1_nb0_out, in_1[2], in_1[1], not_4_out);
  and b2b0 (b2b0_out, in_1[2], in_1[0]);
  and b1b0 (b1b0_out, in_1[0], in_1[1]);
  and nb3_nb2_nb0 (nb3_nb2_nb0_out, not_4_out, not_3_out, not_1_out);
  and nb3b1b0 (nb3b1b0_out, in_1[0], in_1[1], not_1_out);
  and nb2_nb1 (nb2_nb1_out, not_3_out, not_2_out);
  and nb3_nb1_nb0 (nb3_nb1_nb0_out, not_1_out, not_2_out, not_4_out);
  and nb3_nb2 (nb3_nb2_out, not_1_out, not_3_out);
  and b3b1 (b3b1_out, in_1[3], in_1[1]);
  and b3b2 (b3b2_out, in_1[3], in_1[2]);
  and b2_nb1b0 (b2_nb1b0_out, in_1[2], not_2_out, in_1[0]);
  and nb3_nb2b1 (nb3_nb2b1_out, not_1_out, not_3_out, in_1[1]);
  and nb3_nb1 (nb3_nb1_out, not_1_out, not_2_out);
  and nb3b0 (nb3b0_out, not_1_out, in_1[0]);
  and nb3b2 (nb3b2_out, not_1_out, in_1[2]);
  and b3b1_2 (b3b1_2_out, in_1[1], in_1[3]);
  or or_1 (A, in_1[3], nb2b1_out, b1_nb0_out, b2_nb1_out);
  or or_2 (B, in_1[3], nb1_nb0_out, b2_nb1_2_out, b2b1_nb0_out);
  or or_3 (C, in_1[3], b2b0_out, b1b0_out, nb3_nb2_nb0_out);
  and nb2_nb1_nb0 (nb2_nb1_nb0_out, not_2_out, not_4_out, not_3_out);
  or or_4 (D, nb3_nb2_out, nb3b1b0_out, nb2_nb1_out, nb3_nb1_nb0_out);
  or or_5 (E, b1_nb0_out, b3b1_out, nb2_nb1_nb0_out, b3b2_out);
  or or_6 (F, in_1[3], b2_nb1b0_out, nb2_nb1_nb0_out, b1_nb0_out, nb3_nb2b1_out);
  or or_7 (G, nb2_nb1_out, nb3_nb1_out, nb3b0_out, nb3b2_out);
  or or_8 (H, b3b2_out, b3b1_2_out);
endmodule
