// Logisim project lab09.circ as structural Verilog: 1 circuit, main circuit main
module main (
  input  Write,
  input  [2:0] Write_Register,
  input  [31:0] in_3,
  input  [2:0] Read_Register_1,
  input  [2:0] Read_Register_2,
  input  Clock,
  output [31:0] Read_Data_1,
  output [31:0] Read_Data_2
);

  wire demultiplexer_1_out0, demultiplexer_1_out1, demultiplexer_1_out2, demultiplexer_1_out3,
       demultiplexer_1_out4, demultiplexer_1_out5, demultiplexer_1_out6, demultiplexer_1_out7, undriven;
  wire [31:0] Reg_1_q, Reg_2_q, Reg_3_q, Reg_4_q, Reg_5_q, Reg_6_q, Reg_7_q, Reg_8_q;

  Demultiplexer #(.select(3)) demultiplexer_1 (
    .out0(demultiplexer_1_out0), .out1(demultiplexer_1_out1), .out2(demultiplexer_1_out2),
    .out3(demultiplexer_1_out3), .out4(demultiplexer_1_out4), .out5(demultiplexer_1_out5),
    .out6(demultiplexer_1_out6), .out7(demultiplexer_1_out7), .in(Write), .sel(Write_Register), .en(undriven));
  Register #(.width(32), .trigger("falling")) Reg_1 (
    .D(in_3), .en(demultiplexer_1_out0), .Q(Reg_1_q), .clk(Clock));  // open: clr
  Register #(.width(32), .trigger("falling")) Reg_2 (
    .D(in_3), .en(demultiplexer_1_out1), .Q(Reg_2_q), .clk(Clock));  // open: clr
  Register #(.width(32), .trigger("falling")) Reg_3 (
    .D(in_3), .en(demultiplexer_1_out2), .Q(Reg_3_q), .clk(Clock));  // open: clr
  Register #(.width(32), .trigger("falling")) Reg_4 (
    .D(in_3), .en(demultiplexer_1_out3), .Q(Reg_4_q), .clk(Clock));  // open: clr
  Register #(.width(32), .trigger("falling")) Reg_5 (
    .D(in_3), .en(demultiplexer_1_out4), .Q(Reg_5_q), .clk(Clock));  // open: clr
  Register #(.width(32), .trigger("falling")) Reg_6 (
    .D(in_3), .en(demultiplexer_1_out5), .Q(Reg_6_q), .clk(Clock));  // open: clr
  Register #(.width(32), .trigger("falling")) Reg_7 (
    .D(in_3), .en(demultiplexer_1_out6), .Q(Reg_7_q), .clk(Clock));  // open: clr
  Register #(.width(32), .trigger("falling")) Reg_8 (
    .D(in_3), .en(demultiplexer_1_out7), .Q(Reg_8_q), .clk(Clock));  // open: clr
  Multiplexer #(.select(3), .width(32)) multiplexer_1 (
    .in0(Reg_1_q), .in1(Reg_2_q), .in2(Reg_3_q), .in3(Reg_4_q), .in4(Reg_5_q), .in5(Reg_6_q), .in6(Reg_7_q),
    .in7(Reg_8_q), .out(Read_Data_1), .sel(Read_Register_1));  // open: en
  Multiplexer #(.select(3), .width(32)) multiplexer_2 (
    .in0(Reg_1_q), .in1(Reg_2_q), .in2(Reg_3_q), .in3(Reg_4_q), .in4(Reg_5_q), .in5(Reg_6_q), .in6(Reg_7_q),
    .in7(Reg_8_q), .out(Read_Data_2), .sel(Read_Register_2));  // open: en
endmodule
