// Logisim project lab10.circ as structural Verilog: 5 circuits, main circuit main
module main (
);

  wire undriven;
  wire [7:0] adder_1_out, multiplexer_1_out, n8_bit_alu_1_result, register_1_q, register_2_q, register_3_q;
  wire [15:0] rom_1_data;

  Adder adder_1 (.a(register_1_q), .b(8'h1), .out(adder_1_out));  // open: cin, cout
  Register register_1 (.D(adder_1_out), .Q(register_1_q), .clk(1'b1));  // open: en, clr
  Adder adder_2 (.b(8'h1));  // open: a, out, cin, cout
  ROM #(.dataWidth(16)) rom_1 (.addr(register_1_q), .data(rom_1_data), .sel(1'b1));
  Fields fields_1 ();  // open: in_1, Immediate, Reg, Op
  Multiplexer #(.width(8)) multiplexer_1 (
    .in0(n8_bit_alu_1_result), .out(multiplexer_1_out), .sel(undriven));  // open: in1, en
  Register register_2 (.D(multiplexer_1_out), .Q(register_2_q));  // open: en, clk, clr
  Register register_3 (.D(multiplexer_1_out), .Q(register_3_q));  // open: en, clk, clr
  _8_bit_ALu u_8_bit_alu_1 (
    .A(register_2_q), .B(register_3_q), .Result(n8_bit_alu_1_result));  // open: A_Invert, BInvert, OP, Zero, Overflow
endmodule

module _8_bit_ALu (
  input  [7:0] A,
  input  [1:0] OP,
  input  A_Invert,
  input  BInvert,
  input  [7:0] B,
  output Zero,
  output [7:0] Result,
  output Overflow
);

  wire n1_bit_alu_1_carry_out, n1_bit_alu_2_carry_out, n1_bit_alu_3_set, n1_bit_alu_4_carry_out,
       n1_bit_alu_5_carry_out, n1_bit_alu_6_carry_out, n1_bit_alu_7_carry_out, n1_bit_alu_8_carry_out,
       or_1_out, xor_1_out;

  _1_bit_ALU u_1_bit_alu_1 (
    .A(A[5]), .B(B[5]), .Less(1'b0), .Ainvert(A_Invert), .Binvert(BInvert), .CarryIn(n1_bit_alu_8_carry_out),
    .Operation(OP), .Carry_Out(n1_bit_alu_1_carry_out), .Result(Result[5]));  // open: Set
  _1_bit_ALU u_1_bit_alu_2 (
    .A(A[6]), .B(B[6]), .Less(1'b0), .Ainvert(A_Invert), .Binvert(BInvert), .CarryIn(n1_bit_alu_1_carry_out),
    .Operation(OP), .Carry_Out(n1_bit_alu_2_carry_out), .Result(Result[6]));  // open: Set
  _1_bit_ALU u_1_bit_alu_3 (
    .A(A[7]), .B(B[7]), .Less(1'b0), .Ainvert(A_Invert), .Binvert(BInvert), .CarryIn(n1_bit_alu_2_carry_out),
    .Operation(OP), .Carry_Out(Overflow), .Result(Result[7]), .Set(n1_bit_alu_3_set));
  _1_bit_ALU u_1_bit_alu_4 (
    .A(A[0]), .B(B[0]), .Less(xor_1_out), .Ainvert(A_Invert), .Binvert(BInvert), .CarryIn(BInvert),
    .Operation(OP), .Carry_Out(n1_bit_alu_4_carry_out), .Result(Result[0]));  // open: Set
  _1_bit_ALU u_1_bit_alu_5 (
    .A(A[1]), .B(B[1]), .Less(1'b0), .Ainvert(A_Invert), .Binvert(BInvert), .CarryIn(n1_bit_alu_4_carry_out),
    .Operation(OP), .Carry_Out(n1_bit_alu_5_carry_out), .Result(Result[1]));  // open: Set
  _1_bit_ALU u_1_bit_alu_6 (
    .A(A[2]), .B(B[2]), .Less(1'b0), .Ainvert(A_Invert), .Binvert(BInvert), .CarryIn(n1_bit_alu_5_carry_out),
    .Operation(OP), .Carry_Out(n1_bit_alu_6_carry_out), .Result(Result[2]));  // open: Set
  _1_bit_ALU u_1_bit_alu_7 (
    .A(A[3]), .B(B[3]), .Less(1'b0), .Ainvert(A_Invert), .Binvert(BInvert), .CarryIn(n1_bit_alu_6_carry_out),
    .Operation(OP), .Carry_Out(n1_bit_alu_7_carry_out), .Result(Result[3]));  // open: Set
  _1_bit_ALU u_1_bit_alu_8 (
    .A(A[4]), .B(B[4]), .Less(1'b0), .Ainvert(A_Invert), .Binvert(BInvert), .CarryIn(n1_bit_alu_7_carry_out),
    .Operation(OP), .Carry_Out(n1_bit_alu_8_carry_out), .Result(Result[4]));  // open: Set
  xor xor_1 (xor_1_out, n1_bit_alu_3_set, Overflow);
  not not_1 (Zero, or_1_out);
  or or_1 (or_1_out, Result[0], Result[1], Result[2], Result[3], Result[4], Result[5], Result[6], Result[7]);
endmodule

module _1_bit_ALU (
  input  Ainvert,
  input  Binvert,
  input  CarryIn,
  input  [1:0] Operation,
  input  A,
  input  B,
  input  Less,
  output Result,
  output Set,
  output Carry_Out
);

  wire and_1_out, multiplexer_1_out, multiplexer_2_out, not_1_out, not_2_out, or_1_out;

  not not_1 (not_1_out, A);
  not not_2 (not_2_out, B);
  Multiplexer multiplexer_1 (.in0(A), .in1(not_1_out), .out(multiplexer_1_out), .sel(Ainvert));  // open: en
  Multiplexer multiplexer_2 (.in0(B), .in1(not_2_out), .out(multiplexer_2_out), .sel(Binvert));  // open: en
  and and_1 (and_1_out, multiplexer_1_out, multiplexer_2_out);
  or or_1 (or_1_out, multiplexer_2_out, multiplexer_1_out);
  Adder #(.width(1)) adder_1 (.a(multiplexer_1_out), .b(multiplexer_2_out), .out(Set), .cin(CarryIn), .cout(Carry_Out));
  Multiplexer #(.select(2)) multiplexer_3 (
    .in0(and_1_out), .in1(or_1_out), .in2(Set), .in3(Less), .out(Result), .sel(Operation));  // open: en
endmodule

module Fields (
  input  [15:0] in_1,
  output [7:0] Immediate,
  output Reg,
  output [3:0] Op
);


  assign Immediate = in_1[7:0];
  assign Op = in_1[15:12];
  assign Reg = in_1[11];
endmodule

module Decoder (
  input  [3:0] in_1,
  output [1:0] ALU,
  output DstMux
);

  wire not_2_out;

  not not_1 (ALU[1], in_1[2]);
  and and_1 (DstMux, ALU[1], not_2_out);
  not not_2 (not_2_out, in_1[1]);

  assign ALU[0] = in_1[0];
endmodule
